# Fritzing sketch model (saved by Fritzing 0.9.3b)

parts:
  Raspberry_Pi1 = Raspberry Pi 2
  S1 = H-Bridge with L298N
  VCC1 = 4 x AAA Battery Mount
  LED1 = RGB LED (com. anode, rbg) [package="5 mm [THT]"]
  M1 = DC Motor
  M2 = DC Motor

nets:
  N1: Raspberry_Pi1.GIPO17, S1.IN3
  N2: Raspberry_Pi1.GIPO27, S1.IN4
  GND: Raspberry_Pi1.GND, S1.GND, VCC1.-, LED1.blue_cathode
  N3: Raspberry_Pi1.GIPO21, LED1.green_cathode
  N4: Raspberry_Pi1.GIPO20, LED1.common_anode
  N5: Raspberry_Pi1.GIPO16, LED1.red_cathode
  N6: Raspberry_Pi1.GIPO24, S1.IN2
  N7: Raspberry_Pi1.GIPO23, S1.IN1
  5V: Raspberry_Pi1.5V, S1.12V, VCC1.+
  N8: S1.M1-01, M2.pin_2
  N9: S1.M1-02, M2.pin_1
  N10: S1.M2-01, M1.pin_2
  N11: S1.M2-02, M1.pin_1

custom parts:
  H-Bridge with L298N: h-bridge
